# Fritzing sketch Distributrice12 (saved by Fritzing 0.9.9b)
circuit board: 28.7199cm x 15.057cm
breadboards: 1

parts:
  JP1 = Header 2 [package=jst-2-pth-ns]
  IR = Camdenboss CTB0158-4 [part_number=CTB0158-4 package=THT]
  EMETTERS = Camdenboss CTB0158-4 [part_number=CTB0158-4 package=THT]
  Optoc2 = TLP621 [package=THT]
  J1 = RJ11 Jack [package=rj11-6]
  J3 = Camdenboss CTB0158-12 [part_number=CTB0158-12 package=THT]
  J4 = RJ11 Jack [package=rj11-6]
  J5 = Camdenboss CTB0158-2 [part_number=CTB0158-2 package=THT]
  330uF = Ceramic Capacitor [capacitance=100nF voltage=35V package="200 mil [THT, multilayer]"]
  R7 = Resistor [tolerance=±5% resistance=500 power=0.25 package=THT]
  R8 = Resistor [tolerance=±5% resistance=500 power=0.25 package=THT]
  R9 = Resistor [tolerance=±5% resistance=220 power=0.25 package=THT]
  R10 = Resistor [tolerance=±5% resistance=1200 power=0.25 package=THT]
  J6 = RJ11 Jack [package=rj11-6]
  J7 = Camdenboss CTB0158-8 [part_number=CTB0158-8 package=THT]
  R14 = Resistor [tolerance=±5% resistance=220 power=0.25 package=THT]
  R15 = Resistor [tolerance=±5% resistance=300 power=0.25 package=THT]
  C4 = Ceramic Capacitor [capacitance=100nF voltage=35V package="200 mil [THT, multilayer]"]
  IC1 = Voltage Regulator [package=78xxl]
  Optoc3 = TLP621 [package=THT]
  J10 = RJ11 Jack [package=rj11-6]
  Optoc4 = TLP621 [package=THT]
  Optoc5 = TLP621 [package=THT]
  R16 = Resistor [tolerance=±5% resistance=220 power=0.25 package=THT]
  R17 = Resistor [tolerance=±5% resistance=220 power=0.25 package=THT]
  R18 = Resistor [tolerance=±5% resistance=220 power=0.25 package=THT]
  R20 = Resistor [tolerance=±5% resistance=4k power=0.25 package=THT]
  R21 = Resistor [tolerance=±5% resistance=8k power=0.25 package=THT]
  R22 = Resistor [tolerance=±5% resistance=4k power=0.25 package=THT]
  J11 = Camdenboss CTB0158-4 [part_number=CTB0158-4 package=THT]
  ESP32 = MH-ET LIVE ESP32 DEVKIT 38 pins
  R23 = Resistor [tolerance=±5% resistance=4k power=0.25 package=THT]
  R24 = Resistor [tolerance=±5% resistance=8k power=0.25 package=THT]
  R25 = Resistor [tolerance=±5% resistance=8k power=0.25 package=THT]
  R27 = Resistor [tolerance=±5% resistance=100k power=0.25 package=THT]
  R28 = Resistor [tolerance=±5% resistance=100k power=0.25 package=THT]
  R29 = Resistor [tolerance=±5% resistance=100k power=0.25 package=THT]
  Optoc6 = TLP621 [package=THT]
  Optoc7 = TLP621 [package=THT]
  Optoc8 = TLP621 [package=THT]
  J12 = RJ11 Jack [package=rj11-6]
  Maluska1 = maluska dil miniaturrelais [part_number="DIL Mini RY" package=THT]
  Q3 = NPN-Transistor [package="TO92 [THT]"]
  R30 = Resistor [tolerance=±5% resistance=220 power=0.25 package=THT]
  Optoc9 = TLP621 [package=THT]
  J13 = RJ11 Jack [package=rj11-6]
  330uF1 = Ceramic Capacitor [capacitance=100nF voltage=35V package="200 mil [THT, multilayer]"]
  J14 = Camdenboss CTB0158-2 [part_number=CTB0158-2 package=THT]
  Maluska2 = maluska dil miniaturrelais [part_number="DIL Mini RY" package=THT]

nets:
  GND: JP1.1, IR.pin2, IR.pin3, EMETTERS.pin2, EMETTERS.pin3, Optoc2.Pin_2, J1.6, J3.pin1, J3.pin3, J3.pin5, J3.pin11, J4.6, J5.pin1, 330uF.0, J6.6, C4.0, IC1.GND, J10.1, R22.Pin_1, J11.pin4, ESP32.GND, R23.Pin_1, J12.1, Maluska1.6, Maluska1.16, Q3.E, Optoc9.Pin_2, J13.6, 330uF1.0, Maluska2.16
  N1: JP1.2, R14.Pin_1
  IR1: IR.pin1, ESP32.IO15
  IR2: IR.pin4, ESP32.IO2
  N2: EMETTERS.pin1, R7.Pin_1
  N3: EMETTERS.pin4, R8.Pin_1
  N4: Optoc2.Pin_1, R9.Pin_1
  N5: Optoc2.Pin_4, J1.1
  N6: Optoc2.Pin_3, J1.5
  ENA+: J3.pin2, ESP32.IO27
  DIR+: J3.pin4, ESP32.IO26
  PUL: J3.pin6, ESP32.IO32
  12v: J3.pin12, J4.1, J5.pin2, R15.Pin_0, Maluska1.8, Maluska2.8
  N7: J4.3, Q3.C
  5v: 330uF.1, R7.Pin_0, R8.Pin_0, C4.1, IC1.OUT, J14.pin2
  opto2: R9.Pin_0, ESP32.IO13
  H_light: R10.Pin_0, ESP32.IO25
  N8: R10.Pin_1, Q3.B
  SDA: J6.1, ESP32.IO21
  SCL: J6.3, ESP32.IO22
  Relay: J7.pin1, Maluska1.4
  Relay2: J7.pin2, Maluska2.4
  I05: J7.pin3, ESP32.IO5
  I18: J7.pin4, ESP32.IO18
  I19: J7.pin5, ESP32.IO19
  I20: J7.pin6, ESP32.RXD0
  I21: J7.pin7, ESP32.TXD0
  I23: J7.pin8, ESP32.IO23
  LED: R14.Pin_0, ESP32.IO33
  N9: R15.Pin_1, IC1.IN, 330uF1.1
  N10: Optoc3.Pin_1, R17.Pin_1
  N11: Optoc3.Pin_2, J10.4
  3V3: Optoc3.Pin_4, Optoc4.Pin_4, Optoc5.Pin_4, ESP32.3V3, Optoc6.Pin_4, Optoc7.Pin_4, Optoc8.Pin_4
  I36: Optoc3.Pin_3, R20.Pin_1, R21.Pin_1, R22.Pin_0, ESP32.SVP
  N12: J10.2, Optoc5.Pin_2
  N13: J10.3, Optoc4.Pin_2
  N14: J10.6, R16.Pin_0, R17.Pin_0, R18.Pin_0
  N15: Optoc4.Pin_1, R18.Pin_1
  N16: Optoc4.Pin_3, R20.Pin_0
  N17: Optoc5.Pin_1, R16.Pin_1
  N18: Optoc5.Pin_3, R21.Pin_0
  I39: J11.pin1, ESP32.SVN
  I34: J11.pin2, ESP32.IO34
  I14: J11.pin3, ESP32.IO14
  opto1: ESP32.IO35, R23.Pin_0, R24.Pin_1, R25.Pin_1, Optoc8.Pin_3
  I12: ESP32.IO12, R30.Pin_0
  N19: ESP32.5V, J14.pin1
  RelayESP2: ESP32.IO17
  I16: ESP32.IO16
  RelayESP1: ESP32.IO4, Maluska1.1
  IO0: ESP32.IO0
  N20: R24.Pin_0, Optoc6.Pin_3
  N21: R25.Pin_0, Optoc7.Pin_3
  N22: R27.Pin_0, R28.Pin_0, R29.Pin_0, J12.6
  N23: R27.Pin_1, Optoc7.Pin_1
  N24: R28.Pin_1, Optoc8.Pin_1
  N25: R29.Pin_1, Optoc6.Pin_1
  N26: Optoc6.Pin_2, J12.2
  N27: Optoc7.Pin_2, J12.3
  N28: Optoc8.Pin_2, J12.4
  N29: R30.Pin_1, Optoc9.Pin_1
  N30: Optoc9.Pin_4, J13.1
  N31: Optoc9.Pin_3, J13.5

notes:
  Feeder v.2
  Tuta MANUEL
  13jul2023
  Tower input
  Tower output
  H_light
  I2C
  EXTRA GPIO
  MOTOR
  POWER SUPPLY
  LED
  JUMPER
  GND

custom parts:
  MH-ET LIVE ESP32 DEVKIT 38 pins: http://mh.nodebb.com/topic/2/mh-et-live-esp32-devkit
